// Logisim project ARM_CPU.circ as structural Verilog
module main (
);

  RegFile regfile_1 ();  // open: cpsrOut, rW, Clk, W, cpsrIn, S, WE, rA, rB, A, B
endmodule

module Decode (
  input  [31:0] Inst
);


  // Other names for the same wires on the sheet: Cond[3:0] = Inst[31:28]; DestReg[3:0] = Inst[15:12];
  //   Format[1:0] = Inst[27:26]; InputReg[3:0] = Inst[19:16]; SCF = Inst[20]; Imm = Inst[25];
  //   OpCode[3:0] = Inst[24:21]; Operand2[11:0] = Inst[11:0]

  // Notes on the sheet:
  //   operand 2
  //   rd
  //   rn
  //   set cond flags
  //   op code
  //   immediate
  //   format
  //   conditional
endmodule

module RegFile (
  input  [31:0] cpsrIn,
  input  S,
  input  [31:0] W,
  input  WE,
  input  Clk,
  input  [3:0] rA,
  input  [3:0] rW,
  input  [3:0] rB,
  output [31:0] cpsrOut,
  output [31:0] A,
  output [31:0] B
);

  wire and_1_out, and_2_out, and_3_out, and_4_out, and_5_out, and_6_out, and_7_out, and_8_out, and_9_out,
       and_10_out, and_11_out, and_12_out, and_13_out, and_14_out, and_15_out, and_16_out, r0, r1, r2, r3,
       r4, r5, r6, r7, r8, r9, r10, r11, r12, r13, r14, r15;
  wire [31:0] a1, a2, a3, a4, ip, lr, pc, sp, v1, v2, v3, v4, v5, v6, v7, v8;

  Decoder #(.select(4), .enable("false")) decoder_1 (
    .out0(r0), .out1(r1), .out2(r2), .out3(r3), .out4(r4), .out5(r5), .out6(r6), .out7(r7), .out8(r8),
    .out9(r9), .out10(r10), .out11(r11), .out12(r12), .out13(r13), .out14(r14), .out15(r15), .sel(rW));
  Register #(.width(32)) cpsr (.D(cpsrIn), .en(S), .clk(Clk), .Q(cpsrOut));  // open: clr
  Register #(.width(32)) u_a1 (.D(W), .en(and_1_out), .clk(Clk), .Q(a1));  // open: clr
  and and_1 (and_1_out, WE, r0);
  Register #(.width(32)) u_a2 (.D(W), .en(and_2_out), .clk(Clk), .Q(a2));  // open: clr
  and and_2 (and_2_out, WE, r1);
  Register #(.width(32)) u_a3 (.D(W), .en(and_3_out), .clk(Clk), .Q(a3));  // open: clr
  and and_3 (and_3_out, WE, r2);
  Register #(.width(32)) u_a4 (.D(W), .en(and_4_out), .clk(Clk), .Q(a4));  // open: clr
  and and_4 (and_4_out, WE, r3);
  Register #(.width(32)) u_v1 (.D(W), .en(and_5_out), .clk(Clk), .Q(v1));  // open: clr
  and and_5 (and_5_out, WE, r4);
  Register #(.width(32)) u_v2 (.D(W), .en(and_6_out), .clk(Clk), .Q(v2));  // open: clr
  and and_6 (and_6_out, WE, r5);
  Register #(.width(32)) u_v3 (.D(W), .en(and_7_out), .clk(Clk), .Q(v3));  // open: clr
  and and_7 (and_7_out, WE, r6);
  Register #(.width(32)) u_v4 (.D(W), .en(and_8_out), .clk(Clk), .Q(v4));  // open: clr
  and and_8 (and_8_out, WE, r7);
  Register #(.width(32)) u_v5 (.D(W), .en(and_9_out), .clk(Clk), .Q(v5));  // open: clr
  and and_9 (and_9_out, WE, r8);
  Register #(.width(32)) u_v6 (.D(W), .en(and_10_out), .clk(Clk), .Q(v6));  // open: clr
  and and_10 (and_10_out, WE, r9);
  Register #(.width(32)) u_v7 (.D(W), .en(and_11_out), .clk(Clk), .Q(v7));  // open: clr
  and and_11 (and_11_out, WE, r10);
  Register #(.width(32)) u_v8 (.D(W), .en(and_12_out), .clk(Clk), .Q(v8));  // open: clr
  and and_12 (and_12_out, WE, r11);
  Register #(.width(32)) u_ip (.D(W), .en(and_13_out), .clk(Clk), .Q(ip));  // open: clr
  and and_13 (and_13_out, WE, r12);
  Register #(.width(32)) u_sp (.D(W), .en(and_14_out), .clk(Clk), .Q(sp));  // open: clr
  and and_14 (and_14_out, WE, r13);
  Register #(.width(32)) u_lr (.D(W), .en(and_15_out), .clk(Clk), .Q(lr));  // open: clr
  and and_15 (and_15_out, WE, r14);
  Register #(.width(32)) u_pc (.D(W), .en(and_16_out), .clk(Clk), .Q(pc));  // open: clr
  and and_16 (and_16_out, WE, r15);
  Multiplexer #(.select(4), .width(32), .enable("false")) multiplexer_1 (
    .in0(a1), .in1(a2), .in2(a3), .in3(a4), .in4(v1), .in5(v2), .in6(v3), .in7(v4), .in8(v5), .in9(v6),
    .in10(v7), .in11(v8), .in12(ip), .in13(sp), .in14(lr), .in15(pc), .out(A), .sel(rA));
  Multiplexer #(.select(4), .width(32), .enable("false")) multiplexer_2 (
    .in0(a1), .in1(a2), .in2(a3), .in3(a4), .in4(v1), .in5(v2), .in6(v3), .in7(v4), .in8(v5), .in9(v6),
    .in10(v7), .in11(v8), .in12(ip), .in13(sp), .in14(lr), .in15(pc), .out(B), .sel(rB));
endmodule

module csprFlagDecode (
  input  [31:0] Cspr,
  input  [3:0] Cond,
  output Execute
);

  Decoder #(.select(4), .enable("false")) decoder_1 (.sel(Cond));  // open: out0, out1, out2, out3, out4, out5, out6, out7, out8, out9, out10, out11, out12, out13, out14, out15
  // AND_Gate and_1 is placed but not wired
endmodule
